# Fritzing sketch ir_circuit (saved by Fritzing 0.9.2b)
breadboards: 1

parts:
  Part1 = Infra red receiver [part_number="OUT (gpio45) | GND | vcc(3-5v)"]
  Led_IR = smd LED [color="Infrared (940nm)" package="0603 [SMD]"]
  R1 = Resistor [tolerance=±5% resistance=470 package="0603 [SMD]"]
  R2 = Resistor [tolerance=±5% resistance=10 package="0603 [SMD]"]
  BC547 = PNP-Transistor [package="TO92 [THT]"]
  Raspberry_Pi_1 = Raspberry Pi 3

nets:
  GND: Part1.GND, BC547.E, Raspberry_Pi_1.GPIO3, Raspberry_Pi_1.GND
  VCC: Part1.VCC, R2.Pin_0, Raspberry_Pi_1.3v3, Raspberry_Pi_1.5V
  N1: Part1.Data, Raspberry_Pi_1.GIPO18
  N2: Led_IR.cathode, BC547.C
  N3: Led_IR.anode, R2.Pin_1
  N4: R1.Pin_0, BC547.B
  N5: R1.Pin_1, Raspberry_Pi_1.GIPO12

notes:
  VS1838b
